// Logisim project Multiplicador.circ as structural Verilog: 8 circuits, main circuit Soma_1_bit
module Mult_1_byte (
  input  in_1,
  input  in_2,
  input  in_3,
  input  in_4,
  input  in_5,
  input  in_6,
  input  in_7,
  input  in_8,
  input  User_Mode,
  input  in_10,
  input  in_11,
  input  in_12,
  input  in_13,
  input  in_14,
  input  in_15,
  input  in_16,
  input  in_17,
  output out_18,
  output out_19,
  output out_20,
  output out_21,
  output out_22,
  output out_23,
  output out_24,
  output out_25
);

  wire and_1_out, and_2_out, clock_1_out, contador_1_finish, logica_de_controle_1_ate,
       logica_de_controle_1_awe, logica_de_controle_1_cont, logica_de_controle_1_qte,
       logica_de_controle_1_qwe, not_1_out, or_1_out, Registrador_A_s0, Registrador_A_s1, Registrador_A_s2,
       Registrador_A_s3, Registrador_A_s4, Registrador_A_s5, Registrador_A_s6, Registrador_A_s7,
       Registrador_M_s0, Registrador_M_s1, Registrador_M_s2, Registrador_M_s3, Registrador_M_s4,
       Registrador_M_s5, Registrador_M_s6, Registrador_M_s7, soma_8_bits_1_c_out, soma_8_bits_1_s0,
       soma_8_bits_1_s1, soma_8_bits_1_s2, soma_8_bits_1_s3, soma_8_bits_1_s4, soma_8_bits_1_s5,
       soma_8_bits_1_s6, soma_8_bits_1_s7;
  wire [3:0] contador_1_display;

  Clock clock_1 (.out(clock_1_out));
  not not_1 (not_1_out, contador_1_finish);
  and and_1 (and_1_out, clock_1_out, not_1_out);
  Reg_1_byte Registrador_M (
    .D7(in_1), .D6(in_2), .D5(in_3), .D4(in_4), .D3(in_5), .D2(in_6), .D1(in_7), .D0(in_8), .WE(User_Mode),
    .Clock(and_1_out), .S7(Registrador_M_s7), .S6(Registrador_M_s6), .S5(Registrador_M_s5),
    .S4(Registrador_M_s4), .S3(Registrador_M_s3), .S2(Registrador_M_s2), .S1(Registrador_M_s1),
    .S0(Registrador_M_s0));
  Soma_8_bits soma_8_bits_1 (
    .A5(Registrador_M_s5), .B5(Registrador_A_s5), .A4(Registrador_M_s4), .B4(Registrador_A_s4),
    .A3(Registrador_M_s3), .B3(Registrador_A_s3), .A2(Registrador_M_s2), .B2(Registrador_A_s2),
    .A1(Registrador_M_s1), .B1(Registrador_A_s1), .A0(Registrador_M_s0), .B0(Registrador_A_s0), .C_in(1'b0),
    .A7(Registrador_M_s7), .B7(Registrador_A_s7), .A6(Registrador_M_s6), .B6(Registrador_A_s6),
    .S4(soma_8_bits_1_s4), .S3(soma_8_bits_1_s3), .S2(soma_8_bits_1_s2), .S1(soma_8_bits_1_s1),
    .S0(soma_8_bits_1_s0), .C_out(soma_8_bits_1_c_out), .S7(soma_8_bits_1_s7), .S6(soma_8_bits_1_s6),
    .S5(soma_8_bits_1_s5));
  Reg_deslocamento Registrador_A (
    .D7(soma_8_bits_1_s7), .D6(soma_8_bits_1_s6), .D5(soma_8_bits_1_s5), .D4(soma_8_bits_1_s4),
    .D3(soma_8_bits_1_s3), .D2(soma_8_bits_1_s2), .D1(soma_8_bits_1_s1), .D0(soma_8_bits_1_s0),
    .TrEn(logica_de_controle_1_ate), .WE(logica_de_controle_1_awe), .Ex(soma_8_bits_1_c_out), .Ck(and_1_out),
    .Clear(User_Mode), .S7(Registrador_A_s7), .S6(Registrador_A_s6), .S5(Registrador_A_s5),
    .S4(Registrador_A_s4), .S3(Registrador_A_s3), .S2(Registrador_A_s2), .S1(Registrador_A_s1),
    .S0(Registrador_A_s0));
  or or_1 (or_1_out, Registrador_A_s7, Registrador_A_s6, Registrador_A_s5, Registrador_A_s4, Registrador_A_s3, Registrador_A_s2, Registrador_A_s1, Registrador_A_s0);
  // Probe on contador_1_display
  Reg_deslocamento Registrador_Q (
    .D7(in_10), .D6(in_11), .D5(in_12), .D4(in_13), .D3(in_14), .D2(in_15), .D1(in_16), .D0(in_17),
    .TrEn(logica_de_controle_1_qte), .WE(logica_de_controle_1_qwe), .Ex(Registrador_A_s0), .Ck(and_1_out),
    .S7(out_18), .S6(out_19), .S5(out_20), .S4(out_21), .S3(out_22), .S2(out_23), .S1(out_24), .S0(out_25));  // open: Clear
  Logica_de_Controle logica_de_controle_1 (
    .Q0(out_25), .User_Mode(User_Mode), .Clock(and_1_out), .AWE(logica_de_controle_1_awe),
    .ATE(logica_de_controle_1_ate), .QTE(logica_de_controle_1_qte), .CONT(logica_de_controle_1_cont),
    .QWE(logica_de_controle_1_qwe));
  Contador contador_1 (
    .RESET(User_Mode), .COUNT(logica_de_controle_1_cont), .FINISH(contador_1_finish),
    .DISPLAY(contador_1_display));
  and and_2 (and_2_out, contador_1_finish, or_1_out);
  LED OVERFLOW (.in(and_2_out));
  LED FINISH (.in(contador_1_finish));
endmodule

module Soma_1_bit (
  input  A,
  input  B,
  input  C_in,
  output Sum,
  output C_out
);

  wire and_1_out, and_2_out, xor_2_out;

  xor xor_1 (Sum, xor_2_out, C_in);
  xor xor_2 (xor_2_out, A, B);
  and and_1 (and_1_out, C_in, xor_2_out);
  or or_1 (C_out, and_1_out, and_2_out);
  and and_2 (and_2_out, B, A);
endmodule

module Soma_8_bits (
  input  A7,
  input  B7,
  input  A6,
  input  B6,
  input  A5,
  input  B5,
  input  A4,
  input  B4,
  input  A3,
  input  B3,
  input  A2,
  input  B2,
  input  A1,
  input  B1,
  input  A0,
  input  B0,
  input  C_in,
  output C_out,
  output S7,
  output S6,
  output S5,
  output S4,
  output S3,
  output S2,
  output S1,
  output S0
);

  wire soma_1_bit_2_c_out, soma_1_bit_3_c_out, soma_1_bit_4_c_out, soma_1_bit_5_c_out, soma_1_bit_6_c_out,
       soma_1_bit_7_c_out, soma_1_bit_8_c_out;

  Soma_1_bit soma_1_bit_1 (.A(A7), .B(B7), .C_in(soma_1_bit_2_c_out), .Sum(S7), .C_out(C_out));
  Soma_1_bit soma_1_bit_2 (.A(A6), .B(B6), .C_in(soma_1_bit_3_c_out), .Sum(S6), .C_out(soma_1_bit_2_c_out));
  Soma_1_bit soma_1_bit_3 (.A(A5), .B(B5), .C_in(soma_1_bit_4_c_out), .Sum(S5), .C_out(soma_1_bit_3_c_out));
  Soma_1_bit soma_1_bit_4 (.A(A4), .B(B4), .C_in(soma_1_bit_5_c_out), .Sum(S4), .C_out(soma_1_bit_4_c_out));
  Soma_1_bit soma_1_bit_5 (.A(A3), .B(B3), .C_in(soma_1_bit_6_c_out), .Sum(S3), .C_out(soma_1_bit_5_c_out));
  Soma_1_bit soma_1_bit_6 (.A(A2), .B(B2), .C_in(soma_1_bit_7_c_out), .Sum(S2), .C_out(soma_1_bit_6_c_out));
  Soma_1_bit soma_1_bit_7 (.A(A1), .B(B1), .C_in(soma_1_bit_8_c_out), .Sum(S1), .C_out(soma_1_bit_7_c_out));
  Soma_1_bit soma_1_bit_8 (.A(A0), .B(B0), .C_in(C_in), .Sum(S0), .C_out(soma_1_bit_8_c_out));
endmodule

module Reg_1_byte (
  input  D7,
  input  D6,
  input  D5,
  input  D4,
  input  D3,
  input  D2,
  input  D1,
  input  D0,
  input  WE,
  input  Clock,
  output S7,
  output S6,
  output S5,
  output S4,
  output S3,
  output S2,
  output S1,
  output S0
);

  Register #(.width(1)) register_1 (.D(D7), .en(WE), .clk(Clock), .Q(S7), .clr(1'b0));
  Register #(.width(1)) register_2 (.D(D6), .en(WE), .clk(Clock), .Q(S6), .clr(1'b0));
  Register #(.width(1)) register_3 (.D(D5), .en(WE), .clk(Clock), .Q(S5), .clr(1'b0));
  Register #(.width(1)) register_4 (.D(D4), .en(WE), .clk(Clock), .Q(S4), .clr(1'b0));
  Register #(.width(1)) register_5 (.D(D3), .en(WE), .clk(Clock), .Q(S3), .clr(1'b0));
  Register #(.width(1)) register_6 (.D(D2), .en(WE), .clk(Clock), .Q(S2), .clr(1'b0));
  Register #(.width(1)) register_7 (.D(D1), .en(WE), .clk(Clock), .Q(S1), .clr(1'b0));
  Register #(.width(1)) register_8 (.D(D0), .en(WE), .clk(Clock), .Q(S0), .clr(1'b0));
endmodule

module Reg_deslocamento (
  input  D7,
  input  D6,
  input  D5,
  input  D4,
  input  D3,
  input  D2,
  input  D1,
  input  D0,
  input  TrEn,
  input  WE,
  input  Ex,
  input  Ck,
  input  Clear,
  output S7,
  output S6,
  output S5,
  output S4,
  output S3,
  output S2,
  output S1,
  output S0
);

  wire multiplexer_1_out, multiplexer_2_out, multiplexer_3_out, multiplexer_4_out, multiplexer_5_out,
       multiplexer_6_out, multiplexer_7_out, multiplexer_8_out;

  Multiplexer multiplexer_1 (.in0(D7), .in1(Ex), .out(multiplexer_1_out), .sel(TrEn));
  Register #(.width(1)) register_1 (.D(multiplexer_1_out), .en(WE), .clk(Ck), .Q(S7), .clr(Clear));
  Multiplexer multiplexer_2 (.in0(D6), .in1(S7), .out(multiplexer_2_out), .sel(TrEn));
  Register #(.width(1)) register_2 (.D(multiplexer_2_out), .en(WE), .clk(Ck), .Q(S6), .clr(Clear));
  Multiplexer multiplexer_3 (.in0(D5), .in1(S6), .out(multiplexer_3_out), .sel(TrEn));
  Register #(.width(1)) register_3 (.D(multiplexer_3_out), .en(WE), .clk(Ck), .Q(S5), .clr(Clear));
  Multiplexer multiplexer_4 (.in0(D4), .in1(S5), .out(multiplexer_4_out), .sel(TrEn));
  Register #(.width(1)) register_4 (.D(multiplexer_4_out), .en(WE), .clk(Ck), .Q(S4), .clr(Clear));
  Multiplexer multiplexer_5 (.in0(D3), .in1(S4), .out(multiplexer_5_out), .sel(TrEn));
  Register #(.width(1)) register_5 (.D(multiplexer_5_out), .en(WE), .clk(Ck), .Q(S3), .clr(Clear));
  Multiplexer multiplexer_6 (.in0(D2), .in1(S3), .out(multiplexer_6_out), .sel(TrEn));
  Register #(.width(1)) register_6 (.D(multiplexer_6_out), .en(WE), .clk(Ck), .Q(S2), .clr(Clear));
  Multiplexer multiplexer_7 (.in0(D1), .in1(S2), .out(multiplexer_7_out), .sel(TrEn));
  Register #(.width(1)) register_7 (.D(multiplexer_7_out), .en(WE), .clk(Ck), .Q(S1), .clr(Clear));
  Multiplexer multiplexer_8 (.in0(D0), .in1(S1), .out(multiplexer_8_out), .sel(TrEn));
  Register #(.width(1)) register_8 (.D(multiplexer_8_out), .en(WE), .clk(Ck), .Q(S0), .clr(Clear));
endmodule

module Logica_de_Controle (
  input  Q0,
  input  User_Mode,
  input  Clock,
  output AWE,
  output ATE,
  output QTE,
  output CONT,
  output QWE
);

  wire and_1_out, d_ff_1_q, d_ff_2_qn, d_ff_3_q, decode_4x2_1_s0, decode_4x2_1_s1, decode_4x2_1_s2,
       decode_4x2_1_s3, not_1_out, not_2_out, not_3_out, not_4_out, not_5_out, or_1_out, or_2_out, or_3_out,
       or_4_out;

  not not_1 (not_1_out, User_Mode);
  or or_1 (or_1_out, decode_4x2_1_s3, decode_4x2_1_s0);
  or or_2 (or_2_out, or_1_out, and_1_out);
  and and_1 (and_1_out, not_2_out, decode_4x2_1_s1);
  not not_2 (not_2_out, Q0);
  D_Flip_Flop d_ff_1 (.D(not_3_out), .clk(Clock), .Q(d_ff_1_q), .reset(User_Mode));  // open: Qn, preset
  not not_3 (not_3_out, d_ff_1_q);
  D_Flip_Flop d_ff_2 (.clk(Clock), .Qn(d_ff_2_qn), .preset(User_Mode), .reset(or_3_out));  // open: D, Q
  D_Flip_Flop d_ff_3 (.D(or_2_out), .clk(Clock), .Q(d_ff_3_q), .preset(User_Mode));  // open: Qn, reset
  not not_4 (not_4_out, d_ff_3_q);
  DECODE_4X2 decode_4x2_1 (
    .A1(d_ff_1_q), .A0(not_5_out), .S0(decode_4x2_1_s0), .S1(decode_4x2_1_s1), .S2(decode_4x2_1_s2),
    .S3(decode_4x2_1_s3));
  not not_5 (not_5_out, not_4_out);
  or or_3 (or_3_out, decode_4x2_1_s2, decode_4x2_1_s3);
  or or_4 (or_4_out, decode_4x2_1_s1, decode_4x2_1_s3);
  or or_5 (QWE, decode_4x2_1_s3, User_Mode);
  and and_2 (AWE, not_1_out, d_ff_2_qn, or_3_out);
  and and_3 (ATE, not_1_out, d_ff_2_qn, decode_4x2_1_s3);
  and and_4 (QTE, not_1_out, d_ff_2_qn, or_4_out);
  and and_5 (CONT, not_1_out, d_ff_2_qn, decode_4x2_1_s1);

  // Notes on the sheet:
  //   CALCULATE_NEW_STATE
  //   STATE_REGISTER
  //   DEBUG
  //   00 = ADD
  //   01 = SWITCH
  //   10 = HOLD_REGISTER_A
  //   11 = HOLD_ALL
  //   INITIAL_STATE_FALSE
  //   ADD: FALSE
  //   SWITCH: QtrEn, Cont
  //   HOLD_A: AWE
  //   HOLD_ALL: AWE, ATrEn, QWE, QtrEn
endmodule

module DECODE_4X2 (
  input  A1,
  input  A0,
  output S0,
  output S1,
  output S2,
  output S3
);

  wire not_1_out, not_2_out, not_3_out, not_4_out;

  not not_1 (not_1_out, A1);
  not not_2 (not_2_out, A0);
  not not_3 (not_3_out, A1);
  not not_4 (not_4_out, A0);
  and and_1 (S0, not_1_out, not_2_out);
  and and_2 (S1, not_3_out, A0);
  and and_3 (S2, A1, not_4_out);
  and and_4 (S3, A1, A0);
endmodule

module Contador (
  input  RESET,
  input  COUNT,
  output FINISH,
  output [3:0] DISPLAY
);

  wire t_ff_1_qn, t_ff_2_qn, t_ff_3_qn, t_ff_4_qn;

  T_Flip_Flop t_ff_1 (.T(1'b1), .clk(COUNT), .Q(DISPLAY[0]), .Qn(t_ff_1_qn), .reset(RESET));  // open: preset
  T_Flip_Flop t_ff_2 (.T(1'b1), .clk(DISPLAY[0]), .Q(DISPLAY[1]), .Qn(t_ff_2_qn), .reset(RESET));  // open: preset
  T_Flip_Flop t_ff_3 (.T(1'b1), .clk(DISPLAY[1]), .Q(DISPLAY[2]), .Qn(t_ff_3_qn), .reset(RESET));  // open: preset
  T_Flip_Flop t_ff_4 (.T(1'b1), .clk(DISPLAY[2]), .Q(DISPLAY[3]), .Qn(t_ff_4_qn), .preset(RESET));  // open: reset
  and and_1 (FINISH, t_ff_4_qn, t_ff_3_qn, t_ff_2_qn, t_ff_1_qn);
endmodule
